// Digital circuit batalha_naval.dig as structural Verilog
module batalha_naval (
  input  in_2,
  input  [9:0] in_3,
  output [7:0] out_1
);

  batalha_naval #(.applicationType("GHDL"), .CodeFile("/home/piva/UFFS/Sistemas/TrabalhoFinal/batalha_naval.vhd")) u_batalha_naval (
    .clock(in_2), .sw(in_3), .ledg(out_1));
endmodule
